# Fritzing sketch schema-pm (saved by Fritzing 0.8.7b)
breadboards: 1

parts:
  Part1 = Arduino Uno (Rev3)
  Mod1 = MQ-7 breakout
  DHT1 = DHT11 Humitidy and Temperature Sensor
  R1 = Resistor [package="2512 [SMD]"]
  R2 = Resistor [package="0402 [SMD]"]
  Part2 = KY-026 Flame Sensor Module [package="Breakout board"]
  J1 = Piezo Speaker
  U2 = ESP8266 NodeMCU LoLin module
  LCD1 = LCD screen
  LCM1602_IIC1 = LCM1602 IIC [part_number="LCM1602 IIC" chip_label="LCM1602 IIC" package="DIP (Dual Inline) [THT]"]

nets:
  N1: Part1.A1, Mod1.AO
  N2: Part1.A2, Part2.D0
  N3: Part1.A4/SDA, LCM1602_IIC1.SDA
  N4: Part1.A5/SCL, LCM1602_IIC1.SCL
  N5: Part1.D12/MISO, J1.pin2
  GND: Part1.GND, Mod1.GND, DHT1.GND, R1.Pin_1, Part2.G, J1.pin1, U2.GND, LCM1602_IIC1.GND
  N6: Part1.D4, DHT1.DATA
  N7: Part1.D5_PWM, U2.D1
  N8: Part1.D6_PWM, R2.Pin_0
  VCC: Part1.5V, Mod1.VCC, DHT1.VDD, Part2.+, LCM1602_IIC1.VCC
  N9: R1.Pin_0, R2.Pin_1, U2.D2
  VSS: LCD1.VSS, LCM1602_IIC1.VSS
  VDD: LCD1.VDD, LCM1602_IIC1.VDD
  N10: LCD1.V0, LCM1602_IIC1.V0
  N11: LCD1.RS, LCM1602_IIC1.RS
  N12: LCD1.R/W, LCM1602_IIC1.RW
  N13: LCD1.E, LCM1602_IIC1.E
  N14: LCD1.DB0, LCM1602_IIC1.D0
  N15: LCD1.DB1, LCM1602_IIC1.D1
  N16: LCD1.DB2, LCM1602_IIC1.D2
  N17: LCD1.DB3, LCM1602_IIC1.D3
  N18: LCD1.DB4, LCM1602_IIC1.D4
  N19: LCD1.DB5, LCM1602_IIC1.D5
  N20: LCD1.DB6, LCM1602_IIC1.D6
  N21: LCD1.DB7, LCM1602_IIC1.D7
  N22: LCD1.LED+, LCM1602_IIC1.A
  N23: LCD1.LED-, LCM1602_IIC1.K

custom parts:
  MQ-7 breakout: MQ-5 gas sensor
  DHT11 Humitidy and Temperature Sensor: DHT11 Humidity and Temperature Sensor
  KY-026 Flame Sensor Module: KEYES KY-026 Arduino Flame Sensor Module reacts iin the presence of fire.
  ESP8266 NodeMCU LoLin module: ESP8266 based NodeMCU
  LCM1602 IIC: I2C-Module to use a 1602 or 2004 LCD on with the wire.h libory Serial LCD Modul
